# Fritzing sketch Hot water Heater Schematic (saved by Fritzing 0.9.2b)
breadboards: 1

parts:
  Part1 = Arduino Nano (Rev3.0) (ICSP)
  J1 = Basic Servo
  Part2 = Real Time Clock Module - DS1307 RTC Breakout Board
  LED1 = LED - 3mm [color="Green (570nm)" package="3 mm [THT]"]
  LED2 = LED - 3mm [color="Red (633nm)" package="3 mm [THT]"]
  S1 = Pushbutton [package="[THT]"]
  S2 = Pushbutton [package="[THT]"]

nets:
  GND: Part1.GND, Part1.A3, Part1.A0, J1.gnd, Part2.GND, LED1.cathode, LED2.cathode, S1.Pin_1, S1.Pin_2, S2.Pin_1, S2.Pin_2
  N1: Part1.D2, Part2.SDA
  N2: Part1.D3, Part2.SCL
  N3: Part1.D4, J1.pulse
  N4: Part1.D5, Part1.A5, S2.Pin_3, S2.Pin_4
  N5: Part1.D6, Part1.A2, S1.Pin_3, S1.Pin_4
  N6: Part1.D12/MISO, LED1.anode
  5V: Part1.5V, J1.vcc, Part2.5V
  N7: Part1.D13/SCK, LED2.anode
